// Logisim project ALU.circ as structural Verilog: 21 circuits, main circuit ALU
module ALU (
  input  [31:0] A,
  input  [31:0] B,
  input  [4:0] Shift,
  input  CarryIn,
  input  [3:0] opcode,
  output [31:0] S,
  output [3:0] Flags
);

  wire ALU_ADC_C, ALU_ADC_N, ALU_ADC_V, ALU_ADC_Z, ALU_AND_C, ALU_AND_N, ALU_AND_V, ALU_AND_Z, ALU_ASR_C,
       ALU_ASR_N, ALU_ASR_V, ALU_ASR_Z, ALU_BIC_C, ALU_BIC_N, ALU_BIC_V, ALU_BIC_Z, ALU_CMN_C, ALU_CMN_N,
       ALU_CMN_V, ALU_CMN_Z, ALU_CMP_C, ALU_CMP_N, ALU_CMP_V, ALU_CMP_Z, ALU_EOR_C, ALU_EOR_N, ALU_EOR_V,
       ALU_EOR_Z, ALU_LSL_C, ALU_LSL_N, ALU_LSL_V, ALU_LSL_Z, ALU_LSR_C, ALU_LSR_N, ALU_LSR_V, ALU_LSR_Z,
       ALU_MUL_C, ALU_MUL_N, ALU_MUL_V, ALU_MUL_Z, ALU_MVN_C, ALU_MVN_N, ALU_MVN_V, ALU_MVN_Z, ALU_ORR_C,
       ALU_ORR_N, ALU_ORR_V, ALU_ORR_Z, ALU_ROR_C, ALU_ROR_N, ALU_ROR_V, ALU_ROR_Z, ALU_RSB_C, ALU_RSB_N,
       ALU_RSB_V, ALU_RSB_Z, ALU_SBC_C, ALU_SBC_N, ALU_SBC_V, ALU_SBC_Z, ALU_TST_C, ALU_TST_N, ALU_TST_V,
       ALU_TST_Z;
  wire [31:0] ALU_ADC_S, ALU_AND_S, ALU_ASR_S, ALU_BIC_S, ALU_CMN_S, ALU_CMP_S, ALU_EOR_S, ALU_LSL_S,
       ALU_LSR_S, ALU_MUL_S, ALU_MVN_S, ALU_ORR_S, ALU_ROR_S, ALU_RSB_S, ALU_SBC_S, ALU_TST_S;

  ALU_AND alu_and_1 (.A(A), .B(B), .S(ALU_AND_S), .Z(ALU_AND_Z), .N(ALU_AND_N), .C(ALU_AND_C), .V(ALU_AND_V));
  ALU_LSL alu_lsl_1 (.A(A), .Shift(Shift), .S(ALU_LSL_S), .Z(ALU_LSL_Z), .N(ALU_LSL_N), .C(ALU_LSL_C), .V(ALU_LSL_V));
  ALU_ASR alu_asr_1 (.A(A), .Shift(Shift), .S(ALU_ASR_S), .Z(ALU_ASR_Z), .N(ALU_ASR_N), .C(ALU_ASR_C), .V(ALU_ASR_V));
  ALU_SBC alu_sbc_1 (
    .A(A), .Cin(CarryIn), .B(B), .S(ALU_SBC_S), .Z(ALU_SBC_Z), .N(ALU_SBC_N), .C(ALU_SBC_C), .V(ALU_SBC_V));
  ALU_TST alu_tst_1 (.A(A), .B(B), .S(ALU_TST_S), .Z(ALU_TST_Z), .N(ALU_TST_N), .C(ALU_TST_C), .V(ALU_TST_V));
  ALU_CMP alu_cmp_1 (
    .A(A), .Cin(CarryIn), .B(B), .S(ALU_CMP_S), .Z(ALU_CMP_Z), .N(ALU_CMP_N), .C(ALU_CMP_C), .V(ALU_CMP_V));
  ALU_ORR alu_orr_1 (.A(A), .B(B), .S(ALU_ORR_S), .Z(ALU_ORR_Z), .N(ALU_ORR_N), .C(ALU_ORR_C), .V(ALU_ORR_V));
  ALU_BIC alu_bic_1 (.A(A), .B(B), .S(ALU_BIC_S), .Z(ALU_BIC_Z), .N(ALU_BIC_N), .C(ALU_BIC_C), .V(ALU_BIC_V));
  ALU_EOR alu_eor_1 (.A(A), .B(B), .S(ALU_EOR_S), .Z(ALU_EOR_Z), .N(ALU_EOR_N), .C(ALU_EOR_C), .V(ALU_EOR_V));
  ALU_LSR alu_lsr_1 (.A(A), .Shift(Shift), .S(ALU_LSR_S), .Z(ALU_LSR_Z), .N(ALU_LSR_N), .C(ALU_LSR_C), .V(ALU_LSR_V));
  ALU_ADC alu_adc_1 (
    .A(A), .Cin(CarryIn), .B(B), .S(ALU_ADC_S), .Z(ALU_ADC_Z), .N(ALU_ADC_N), .C(ALU_ADC_C), .V(ALU_ADC_V));
  ALU_ROR alu_ror_1 (.A(A), .Shift(Shift), .S(ALU_ROR_S), .Z(ALU_ROR_Z), .N(ALU_ROR_N), .C(ALU_ROR_C), .V(ALU_ROR_V));
  ALU_RSB alu_rsb_1 (.A(A), .S(ALU_RSB_S), .Z(ALU_RSB_Z), .N(ALU_RSB_N), .C(ALU_RSB_C), .V(ALU_RSB_V));
  ALU_CMN alu_cmn_1 (
    .A(A), .Cin(CarryIn), .B(B), .S(ALU_CMN_S), .Z(ALU_CMN_Z), .N(ALU_CMN_N), .C(ALU_CMN_C), .V(ALU_CMN_V));
  ALU_MUL alu_mul_1 (.A(A), .B(B), .S(ALU_MUL_S), .Z(ALU_MUL_Z), .N(ALU_MUL_N), .C(ALU_MUL_C), .V(ALU_MUL_V));
  ALU_MVN alu_mvn_1 (.A(A), .S(ALU_MVN_S), .Z(ALU_MVN_Z), .N(ALU_MVN_N), .C(ALU_MVN_C), .V(ALU_MVN_V));
  Multiplexer #(.select(4), .width(32)) multiplexer_1 (
    .in0(ALU_AND_S), .in1(ALU_EOR_S), .in2(ALU_LSL_S), .in3(ALU_LSR_S), .in4(ALU_ASR_S), .in5(ALU_ADC_S),
    .in6(ALU_SBC_S), .in7(ALU_ROR_S), .in8(ALU_TST_S), .in9(ALU_RSB_S), .in10(ALU_CMP_S), .in11(ALU_CMN_S),
    .in12(ALU_ORR_S), .in13(ALU_MUL_S), .in14(ALU_BIC_S), .in15(ALU_MVN_S), .out(S), .sel(opcode));
  Multiplexer #(.select(4)) multiplexer_2 (
    .in0(ALU_AND_N), .in1(ALU_EOR_N), .in2(ALU_LSL_N), .in3(ALU_LSR_N), .in4(ALU_ASR_N), .in5(ALU_ADC_N),
    .in6(ALU_SBC_N), .in7(ALU_ROR_N), .in8(ALU_TST_N), .in9(ALU_RSB_N), .in10(ALU_CMP_N), .in11(ALU_CMN_N),
    .in12(ALU_ORR_N), .in13(ALU_MUL_N), .in14(ALU_BIC_N), .in15(ALU_MVN_N), .out(Flags[3]), .sel(opcode));
  Multiplexer #(.select(4)) multiplexer_3 (
    .in0(ALU_AND_Z), .in1(ALU_EOR_Z), .in2(ALU_LSL_Z), .in3(ALU_LSR_Z), .in4(ALU_ASR_Z), .in5(ALU_ADC_Z),
    .in6(ALU_SBC_Z), .in7(ALU_ROR_Z), .in8(ALU_TST_Z), .in9(ALU_RSB_Z), .in10(ALU_CMP_Z), .in11(ALU_CMN_Z),
    .in12(ALU_ORR_Z), .in13(ALU_MUL_Z), .in14(ALU_BIC_Z), .in15(ALU_MVN_Z), .out(Flags[2]), .sel(opcode));
  Multiplexer #(.select(4)) multiplexer_4 (
    .in0(ALU_AND_C), .in1(ALU_EOR_C), .in2(ALU_LSL_C), .in3(ALU_LSR_C), .in4(ALU_ASR_C), .in5(ALU_ADC_C),
    .in6(ALU_SBC_C), .in7(ALU_ROR_C), .in8(ALU_TST_C), .in9(ALU_RSB_C), .in10(ALU_CMP_C), .in11(ALU_CMN_C),
    .in12(ALU_ORR_C), .in13(ALU_MUL_C), .in14(ALU_BIC_C), .in15(ALU_MVN_C), .out(Flags[1]), .sel(opcode));
  Multiplexer #(.select(4)) multiplexer_5 (
    .in0(ALU_AND_V), .in1(ALU_EOR_V), .in2(ALU_LSL_V), .in3(ALU_LSR_V), .in4(ALU_ASR_V), .in5(ALU_ADC_V),
    .in6(ALU_SBC_V), .in7(ALU_ROR_V), .in8(ALU_TST_V), .in9(ALU_RSB_V), .in10(ALU_CMP_V), .in11(ALU_CMN_V),
    .in12(ALU_ORR_V), .in13(ALU_MUL_V), .in14(ALU_BIC_V), .in15(ALU_MVN_V), .out(Flags[0]), .sel(opcode));

  // Other names for the same wires on the sheet: Cin = CarryIn; V = Flags[0]; C = Flags[1]; Z = Flags[2];
  //   N = Flags[3]
endmodule

module Z_flag (
  input  [31:0] I,
  output O
);

  wire and_1_out, and_2_out;
  wire [3:0] nor_1_out, nor_2_out;

  assign nor_1_out = ~(I[3:0] | I[7:4] | I[11:8] | I[15:12]);  // NOR_Gate nor_1, 4 bits wide
  assign nor_2_out = ~(I[19:16] | I[23:20] | I[27:24] | I[31:28]);  // NOR_Gate nor_2, 4 bits wide
  and and_1 (and_1_out, nor_1_out[0], nor_1_out[1], nor_1_out[2], nor_1_out[3]);
  and and_2 (and_2_out, nor_2_out[0], nor_2_out[1], nor_2_out[2], nor_2_out[3]);
  and and_3 (O, and_1_out, and_2_out);
endmodule

module N_flag (
  input  [31:0] I,
  output O
);

  BitSelector #(.width(32)) bitselector_1 (.in(I), .out(O), .sel({5{1'b1}}));
endmodule

module ALU_AND (
  input  [31:0] A,
  input  [31:0] B,
  output [31:0] S,
  output Z,
  output N,
  output C,
  output V
);

  assign S = A & B;  // AND_Gate and_1, 32 bits wide
  ignore_1b ignore_1b_1 (.out_1(V));
  Z_flag z_flag_1 (.I(S), .O(Z));
  N_flag n_flag_1 (.I(S), .O(N));

  assign C = 1'b0;
endmodule

module ALU_EOR (
  input  [31:0] A,
  input  [31:0] B,
  output [31:0] S,
  output Z,
  output N,
  output C,
  output V
);

  wire [31:0] and_1_out, and_2_out, not_1_out, not_2_out;

  assign and_1_out = A & not_1_out;  // AND_Gate and_1, 32 bits wide
  assign not_1_out = ~B;  // NOT_Gate not_1, 32 bits wide
  assign not_2_out = ~A;  // NOT_Gate not_2, 32 bits wide
  assign and_2_out = not_2_out & B;  // AND_Gate and_2, 32 bits wide
  assign S = and_1_out | and_2_out;  // OR_Gate or_1, 32 bits wide
  Z_flag z_flag_1 (.I(S), .O(Z));
  N_flag n_flag_1 (.I(S), .O(N));
  ignore_1b ignore_1b_1 (.out_1(V));

  assign C = 1'b0;
endmodule

module ALU_LSL (
  input  [31:0] A,
  input  [4:0] Shift,
  output [31:0] S,
  output Z,
  output N,
  output C,
  output V
);

  wire bitselector_1_out, nor_1_out;
  wire [4:0] subtractor_1_out;

  Shifter #(.width(32)) shifter_1 (.in(A), .\dist (Shift), .out(S));
  BitSelector #(.width(32)) bitselector_1 (.in(A), .out(bitselector_1_out), .sel(subtractor_1_out));
  Subtractor #(.width(5)) subtractor_1 (.a({5{1'b0}}), .b(Shift), .out(subtractor_1_out));  // open: bin, bout
  ignore_1b ignore_1b_1 (.out_1(V));
  Z_flag z_flag_1 (.I(S), .O(Z));
  N_flag n_flag_1 (.I(S), .O(N));
  Multiplexer multiplexer_1 (.in0(bitselector_1_out), .in1(1'b0), .out(C), .sel(nor_1_out));
  nor nor_1 (nor_1_out, Shift[4], Shift[3], Shift[2], Shift[1], Shift[0]);

  // Other names for the same wires on the sheet: s_t[4:0] = Shift
endmodule

module ALU_LSR (
  input  [31:0] A,
  input  [4:0] Shift,
  output [31:0] S,
  output Z,
  output N,
  output C,
  output V
);

  wire [4:0] subtractor_1_out;

  Shifter #(.shift("lr"), .width(32)) shifter_1 (.in(A), .\dist (Shift), .out(S));
  Subtractor #(.width(5)) subtractor_1 (.a(Shift), .b(5'b00001), .out(subtractor_1_out));  // open: bin, bout
  ignore_1b ignore_1b_1 (.out_1(V));
  Z_flag z_flag_1 (.I(S), .O(Z));
  N_flag n_flag_1 (.I(S), .O(N));
  BitSelector #(.width(32)) bitselector_1 (.in(A), .out(C), .sel(subtractor_1_out));
endmodule

module ALU_ASR (
  input  [31:0] A,
  input  [4:0] Shift,
  output [31:0] S,
  output Z,
  output N,
  output C,
  output V
);

  wire [4:0] subtractor_1_out;

  Shifter #(.shift("ar"), .width(32)) shifter_1 (.in(A), .\dist (Shift), .out(S));
  Subtractor #(.width(5)) subtractor_1 (.a(Shift), .b(5'b00001), .out(subtractor_1_out));  // open: bin, bout
  ignore_1b ignore_1b_1 (.out_1(V));
  Z_flag z_flag_1 (.I(S), .O(Z));
  N_flag n_flag_1 (.I(S), .O(N));
  BitSelector #(.width(32)) bitselector_1 (.in(A), .out(C), .sel(subtractor_1_out));
endmodule

module ALU_ADC (
  input  [31:0] A,
  input  Cin,
  input  [31:0] B,
  output [31:0] S,
  output Z,
  output N,
  output C,
  output V
);

  wire and_1_out, and_2_out, and_3_out, and_4_out, n_flag_1_o, n_flag_2_o, not_1_out, not_2_out, not_3_out;

  not not_1 (not_1_out, n_flag_1_o);
  not not_2 (not_2_out, n_flag_2_o);
  and and_1 (and_1_out, not_1_out, not_2_out);
  N_flag n_flag_1 (.I(A), .O(n_flag_1_o));
  N_flag n_flag_2 (.I(B), .O(n_flag_2_o));
  and and_2 (and_2_out, n_flag_1_o, n_flag_2_o);
  Adder #(.width(32)) adder_1 (.a(A), .b(B), .out(S), .cin(Cin), .cout(C));
  Z_flag z_flag_1 (.I(S), .O(Z));
  N_flag n_flag_3 (.I(S), .O(N));
  not not_3 (not_3_out, N);
  and and_3 (and_3_out, not_3_out, and_2_out);
  and and_4 (and_4_out, N, and_1_out);
  or or_1 (V, and_3_out, and_4_out);
endmodule

module ALU_SBC (
  input  [31:0] A,
  input  Cin,
  input  [31:0] B,
  output [31:0] S,
  output Z,
  output N,
  output C,
  output V
);

  wire and_1_out, and_2_out, and_3_out, and_4_out, n_flag_1_o, n_flag_2_o, not_1_out, not_2_out, not_3_out,
       not_5_out, subtractor_1_bout;

  not not_1 (not_1_out, n_flag_1_o);
  and and_1 (and_1_out, not_1_out, n_flag_2_o);
  N_flag n_flag_1 (.I(A), .O(n_flag_1_o));
  N_flag n_flag_2 (.I(B), .O(n_flag_2_o));
  not not_2 (not_2_out, n_flag_2_o);
  and and_2 (and_2_out, n_flag_1_o, not_2_out);
  not not_3 (not_3_out, Cin);
  Subtractor #(.width(32)) subtractor_1 (.a(A), .b(B), .out(S), .bin(not_3_out), .bout(subtractor_1_bout));
  Z_flag z_flag_1 (.I(S), .O(Z));
  N_flag n_flag_3 (.I(S), .O(N));
  not not_4 (C, subtractor_1_bout);
  not not_5 (not_5_out, N);
  and and_3 (and_3_out, not_5_out, and_2_out);
  and and_4 (and_4_out, N, and_1_out);
  or or_1 (V, and_3_out, and_4_out);
endmodule

module ALU_ROR (
  input  [31:0] A,
  input  [4:0] Shift,
  output [31:0] S,
  output Z,
  output N,
  output C,
  output V
);

  wire [4:0] subtractor_1_out;
  wire [31:0] shifter_1_out, shifter_2_out;

  Shifter #(.shift("lr"), .width(32)) shifter_1 (.in(A), .\dist (Shift), .out(shifter_1_out));
  Subtractor #(.width(5)) subtractor_1 (.a({5{1'b1}}), .b(Shift), .out(subtractor_1_out));  // open: bin, bout
  assign S = shifter_1_out | shifter_2_out;  // OR_Gate or_1, 32 bits wide
  Shifter #(.width(32)) shifter_2 (.in(A), .\dist (subtractor_1_out), .out(shifter_2_out));
  Z_flag z_flag_1 (.I(S), .O(Z));
  N_flag n_flag_1 (.I(S), .O(C));
  ignore_1b ignore_1b_1 (.out_1(V));

  assign N = C;
endmodule

module ALU_TST (
  input  [31:0] A,
  input  [31:0] B,
  output [31:0] S,
  output Z,
  output N,
  output C,
  output V
);

  wire [31:0] and_1_out;

  ignore_32b ignore_32b_1 (.out_1(S));
  assign and_1_out = A & B;  // AND_Gate and_1, 32 bits wide
  ignore_1b ignore_1b_1 (.out_1(V));
  Z_flag z_flag_1 (.I(and_1_out), .O(Z));
  N_flag n_flag_1 (.I(and_1_out), .O(N));

  assign C = 1'b0;
endmodule

module ALU_RSB (
  input  [31:0] A,
  output [31:0] S,
  output Z,
  output N,
  output C,
  output V
);

  wire n_flag_1_o, not_2_out, not_3_out;
  wire [31:0] adder_1_out, not_1_out;

  Adder #(.width(32)) adder_1 (.a(32'h1), .b(not_1_out), .out(adder_1_out));  // open: cin, cout
  assign not_1_out = ~A;  // NOT_Gate not_1, 32 bits wide
  N_flag n_flag_1 (.I(not_1_out), .O(n_flag_1_o));
  not not_2 (not_2_out, n_flag_1_o);
  ignore_32b ignore_32b_1 (.out_1(S));
  Z_flag z_flag_1 (.I(adder_1_out), .O(Z));
  N_flag n_flag_2 (.I(adder_1_out), .O(N));
  not not_3 (not_3_out, N);
  and and_1 (V, not_3_out, not_2_out);

  assign C = 1'b0;
endmodule

module ALU_CMP (
  input  [31:0] A,
  input  Cin,
  input  [31:0] B,
  output [31:0] S,
  output Z,
  output N,
  output C,
  output V
);

  wire and_1_out, and_2_out, and_3_out, and_4_out, n_flag_1_o, n_flag_2_o, not_1_out, not_2_out, not_3_out,
       not_5_out, subtractor_1_bout;
  wire [31:0] subtractor_1_out;

  not not_1 (not_1_out, n_flag_1_o);
  and and_1 (and_1_out, not_1_out, n_flag_2_o);
  N_flag n_flag_1 (.I(A), .O(n_flag_1_o));
  N_flag n_flag_2 (.I(B), .O(n_flag_2_o));
  not not_2 (not_2_out, n_flag_2_o);
  and and_2 (and_2_out, n_flag_1_o, not_2_out);
  not not_3 (not_3_out, Cin);
  Subtractor #(.width(32)) subtractor_1 (
    .a(A), .b(B), .out(subtractor_1_out), .bin(not_3_out), .bout(subtractor_1_bout));
  ignore_32b ignore_32b_1 (.out_1(S));
  Z_flag z_flag_1 (.I(subtractor_1_out), .O(Z));
  N_flag n_flag_3 (.I(subtractor_1_out), .O(N));
  not not_4 (C, subtractor_1_bout);
  not not_5 (not_5_out, N);
  and and_3 (and_3_out, not_5_out, and_2_out);
  and and_4 (and_4_out, N, and_1_out);
  or or_1 (V, and_3_out, and_4_out);
endmodule

module ALU_CMN (
  input  [31:0] A,
  input  Cin,
  input  [31:0] B,
  output [31:0] S,
  output Z,
  output N,
  output C,
  output V
);

  wire and_1_out, and_2_out, and_3_out, and_4_out, n_flag_1_o, n_flag_2_o, not_1_out, not_2_out, not_3_out;
  wire [31:0] adder_1_out;

  not not_1 (not_1_out, n_flag_1_o);
  not not_2 (not_2_out, n_flag_2_o);
  and and_1 (and_1_out, not_1_out, not_2_out);
  N_flag n_flag_1 (.I(A), .O(n_flag_1_o));
  N_flag n_flag_2 (.I(B), .O(n_flag_2_o));
  and and_2 (and_2_out, n_flag_1_o, n_flag_2_o);
  Adder #(.width(32)) adder_1 (.a(A), .b(B), .out(adder_1_out), .cin(Cin), .cout(C));
  ignore_32b ignore_32b_1 (.out_1(S));
  Z_flag z_flag_1 (.I(adder_1_out), .O(Z));
  N_flag n_flag_3 (.I(adder_1_out), .O(N));
  not not_3 (not_3_out, N);
  and and_3 (and_3_out, not_3_out, and_2_out);
  and and_4 (and_4_out, N, and_1_out);
  or or_1 (V, and_3_out, and_4_out);
endmodule

module ALU_ORR (
  input  [31:0] A,
  input  [31:0] B,
  output [31:0] S,
  output Z,
  output N,
  output C,
  output V
);

  assign S = A | B;  // OR_Gate or_1, 32 bits wide
  ignore_1b ignore_1b_1 (.out_1(V));
  Z_flag z_flag_1 (.I(S), .O(Z));
  N_flag n_flag_1 (.I(S), .O(N));

  assign C = 1'b0;
endmodule

module ALU_MUL (
  input  [31:0] A,
  input  [31:0] B,
  output [31:0] S,
  output Z,
  output N,
  output C,
  output V
);

  Multiplier #(.width(32)) multiplier_1 (.a(A), .b(B), .out(S), .cin({32{1'b0}}));  // open: cout
  ignore_1b ignore_1b_1 (.out_1(C));
  ignore_1b ignore_1b_2 (.out_1(V));
  Z_flag z_flag_1 (.I(S), .O(Z));
  N_flag n_flag_1 (.I(S), .O(N));
endmodule

module ALU_BIC (
  input  [31:0] A,
  input  [31:0] B,
  output [31:0] S,
  output Z,
  output N,
  output C,
  output V
);

  wire [31:0] not_1_out;

  assign not_1_out = ~B;  // NOT_Gate not_1, 32 bits wide
  assign S = A & not_1_out;  // AND_Gate and_1, 32 bits wide
  ignore_1b ignore_1b_1 (.out_1(V));
  Z_flag z_flag_1 (.I(S), .O(Z));
  N_flag n_flag_1 (.I(S), .O(N));

  assign C = 1'b0;
endmodule

module ALU_MVN (
  input  [31:0] A,
  output [31:0] S,
  output Z,
  output N,
  output C,
  output V
);

  assign S = ~A;  // NOT_Gate not_1, 32 bits wide
  ignore_1b ignore_1b_1 (.out_1(V));
  Z_flag z_flag_1 (.I(S), .O(Z));
  N_flag n_flag_1 (.I(S), .O(N));

  assign C = 1'b0;
endmodule

module ignore_1b (
  output out_1
);


  assign out_1 = 1'b0;
endmodule

module ignore_32b (
  output [31:0] out_1
);


  assign out_1 = {32{1'b0}};
endmodule
