// Logisim project BancDeRegistres.circ as structural Verilog: 2 circuits, main circuit BancRegistre
module BancRegistre (
  input  [31:0] DataIn,
  input  [2:0] RegB,
  input  [2:0] RegDest,
  input  [2:0] RegA,
  input  Clk,
  input  Reset,
  output [31:0] R0,
  output [31:0] R1,
  output [31:0] AOut,
  output [31:0] R2,
  output [31:0] R3,
  output [31:0] BOut,
  output [31:0] R4,
  output [31:0] R5,
  output [31:0] R6,
  output [31:0] R7
);

  wire decoder_1_out0, decoder_1_out1, decoder_1_out2, decoder_1_out3, decoder_1_out4, decoder_1_out5,
       decoder_1_out6, decoder_1_out7;
  wire [31:0] register_1_q, register_2_q, register_3_q, register_4_q, register_5_q, register_6_q,
       register_7_q, register_8_q;

  Decoder #(.select(3)) decoder_1 (
    .out0(decoder_1_out0), .out1(decoder_1_out1), .out2(decoder_1_out2), .out3(decoder_1_out3),
    .out4(decoder_1_out4), .out5(decoder_1_out5), .out6(decoder_1_out6), .out7(decoder_1_out7), .sel(RegDest));  // open: en
  Register #(.width(32)) register_1 (.D(DataIn), .en(decoder_1_out0), .clk(Clk), .Q(register_1_q));  // open: clr
  Register #(.width(32)) register_2 (.D(DataIn), .en(decoder_1_out1), .clk(Clk), .Q(register_2_q));  // open: clr
  Register #(.width(32)) register_3 (.D(DataIn), .en(decoder_1_out2), .clk(Clk), .Q(register_3_q));  // open: clr
  Register #(.width(32)) register_4 (.D(DataIn), .en(decoder_1_out3), .clk(Clk), .Q(register_4_q));  // open: clr
  Register #(.width(32)) register_5 (.D(DataIn), .en(decoder_1_out4), .clk(Clk), .Q(register_5_q));  // open: clr
  Register #(.width(32)) register_6 (.D(DataIn), .en(decoder_1_out5), .clk(Clk), .Q(register_6_q));  // open: clr
  Register #(.width(32)) register_7 (.D(DataIn), .en(decoder_1_out6), .clk(Clk), .Q(register_7_q));  // open: clr
  Register #(.width(32)) register_8 (.D(DataIn), .en(decoder_1_out7), .clk(Clk), .Q(register_8_q));  // open: clr
  Multiplexer #(.select(3), .width(32)) multiplexer_1 (
    .in0(register_1_q), .in1(register_2_q), .in2(register_3_q), .in3(register_4_q), .in4(register_5_q),
    .in5(register_6_q), .in6(register_7_q), .in7(register_8_q), .out(AOut));  // open: sel
  Multiplexer #(.select(3), .width(32)) multiplexer_2 (
    .in0(register_1_q), .in1(register_2_q), .in2(register_3_q), .in3(register_4_q), .in4(register_5_q),
    .in5(register_6_q), .in6(register_7_q), .in7(register_8_q), .out(BOut));  // open: sel
  // AND_Gate and_1 is placed but not wired
endmodule

module bascule (
  input  Clk,
  input  E,
  input  in_3,
  input  in_4,
  input  in_5,
  input  in_6,
  input  in_7,
  input  in_8,
  input  in_9,
  input  in_10,
  input  in_11,
  input  in_12,
  input  in_13,
  input  in_14,
  input  in_15,
  input  in_16,
  input  in_17,
  input  in_18,
  input  in_19,
  input  in_20,
  input  in_21,
  input  in_22,
  input  in_23,
  input  in_24,
  input  in_25,
  input  in_26,
  input  in_27,
  input  in_28,
  input  in_29,
  input  in_30,
  input  in_31,
  input  in_32,
  input  in_33,
  input  in_34
);

  D_Flip_Flop d_ff_1 (.D(E), .clk(Clk), .Q(in_4));  // open: Qn, preset, reset
  D_Flip_Flop d_ff_2 (.D(in_4), .clk(Clk), .Q(in_5));  // open: Qn, preset, reset
  D_Flip_Flop d_ff_3 (.D(in_5), .clk(Clk), .Q(in_6));  // open: Qn, preset, reset
  D_Flip_Flop d_ff_4 (.D(in_6), .clk(Clk), .Q(in_7));  // open: Qn, preset, reset
  D_Flip_Flop d_ff_5 (.D(in_7), .clk(Clk), .Q(in_8));  // open: Qn, preset, reset
  D_Flip_Flop d_ff_6 (.D(in_8), .clk(Clk), .Q(in_9));  // open: Qn, preset, reset
  D_Flip_Flop d_ff_7 (.D(in_9), .clk(Clk), .Q(in_10));  // open: Qn, preset, reset
  D_Flip_Flop d_ff_8 (.D(in_10), .clk(Clk), .Q(in_11));  // open: Qn, preset, reset
  D_Flip_Flop d_ff_9 (.D(in_11), .clk(Clk), .Q(in_12));  // open: Qn, preset, reset
  D_Flip_Flop d_ff_10 (.D(in_12), .clk(Clk), .Q(in_13));  // open: Qn, preset, reset
  D_Flip_Flop d_ff_11 (.D(in_13), .clk(Clk), .Q(in_14));  // open: Qn, preset, reset
  D_Flip_Flop d_ff_12 (.D(in_14), .clk(Clk), .Q(in_15));  // open: Qn, preset, reset
  D_Flip_Flop d_ff_13 (.D(in_15), .clk(Clk), .Q(in_16));  // open: Qn, preset, reset
  D_Flip_Flop d_ff_14 (.D(in_16), .clk(Clk), .Q(in_17));  // open: Qn, preset, reset
  D_Flip_Flop d_ff_15 (.D(in_17), .clk(Clk), .Q(in_18));  // open: Qn, preset, reset
  D_Flip_Flop d_ff_16 (.D(in_18), .clk(Clk), .Q(in_19));  // open: Qn, preset, reset
  D_Flip_Flop d_ff_17 (.D(in_19), .clk(Clk), .Q(in_20));  // open: Qn, preset, reset
  D_Flip_Flop d_ff_18 (.D(in_20), .clk(Clk), .Q(in_21));  // open: Qn, preset, reset
  D_Flip_Flop d_ff_19 (.D(in_21), .clk(Clk), .Q(in_22));  // open: Qn, preset, reset
  D_Flip_Flop d_ff_20 (.D(in_22), .clk(Clk), .Q(in_23));  // open: Qn, preset, reset
  D_Flip_Flop d_ff_21 (.D(in_23), .clk(Clk), .Q(in_24));  // open: Qn, preset, reset
  D_Flip_Flop d_ff_22 (.D(in_24), .clk(Clk), .Q(in_25));  // open: Qn, preset, reset
  D_Flip_Flop d_ff_23 (.D(in_25), .clk(Clk), .Q(in_3));  // open: Qn, preset, reset
  D_Flip_Flop d_ff_24 (.D(in_3), .clk(Clk), .Q(in_26));  // open: Qn, preset, reset
  D_Flip_Flop d_ff_25 (.D(in_26), .clk(Clk), .Q(in_27));  // open: Qn, preset, reset
  D_Flip_Flop d_ff_26 (.D(in_27), .clk(Clk), .Q(in_28));  // open: Qn, preset, reset
  D_Flip_Flop d_ff_27 (.D(in_28), .clk(Clk), .Q(in_29));  // open: Qn, preset, reset
  D_Flip_Flop d_ff_28 (.D(in_29), .clk(Clk), .Q(in_30));  // open: Qn, preset, reset
  D_Flip_Flop d_ff_29 (.D(in_30), .clk(Clk), .Q(in_31));  // open: Qn, preset, reset
  D_Flip_Flop d_ff_30 (.D(in_31), .clk(Clk), .Q(in_32));  // open: Qn, preset, reset
  D_Flip_Flop d_ff_31 (.D(in_32), .clk(Clk), .Q(in_33));  // open: Qn, preset, reset
  D_Flip_Flop d_ff_32 (.D(in_33), .clk(Clk), .Q(in_34));  // open: Qn, preset, reset
endmodule
