// Logisim project Ctl_Conditional.circ as structural Verilog: 17 circuits, main circuit Conditional
module Conditional (
  input  Enable,
  input  [15:0] Instruction,
  input  Z,
  input  N,
  input  C,
  input  V,
  output [10:0] Offset,
  output Verified
);

  wire al_1_res, al_2_res, cc_lo_1_res, cs_hs_1_res, eq_1_res, ge_1_res, gt_1_res, hi_1_res, le_1_res,
       ls_1_res, lt_1_res, mi_1_res, multiplexer_2_out, multiplexer_3_out, multiplexer_4_out, ne_1_res,
       nv_1_res, nv_2_res, pl_1_res, vc_1_res, vs_1_res;
  wire [10:0] bit_extender_1_out, bit_extender_2_out, multiplexer_1_out;

  assign bit_extender_1_out = {{3{Instruction[7]}}, Instruction[7:0]};  // Bit_Extender bit_extender_1
  EQ eq_1 (.Z(Z), .Res(eq_1_res));
  NE ne_1 (.Z(Z), .Res(ne_1_res));
  CS_HS cs_hs_1 (.C(C), .Res(cs_hs_1_res));
  CC_LO cc_lo_1 (.C(C), .Res(cc_lo_1_res));
  MI mi_1 (.N(N), .Res(mi_1_res));
  PL pl_1 (.N(N), .Res(pl_1_res));
  VS vs_1 (.V(V), .Res(vs_1_res));
  VC vc_1 (.V(V), .Res(vc_1_res));
  HI hi_1 (.Z(Z), .C(C), .Res(hi_1_res));
  LS ls_1 (.Z(Z), .C(C), .Res(ls_1_res));
  GE ge_1 (.V(V), .N(N), .Res(ge_1_res));
  LT lt_1 (.V(V), .N(N), .Res(lt_1_res));
  GT gt_1 (.N(N), .V(V), .Z(Z), .Res(gt_1_res));
  LE le_1 (.N(N), .V(V), .Z(Z), .Res(le_1_res));
  AL al_1 (.Res(al_1_res));
  NV nv_1 (.Res(nv_1_res));
  Multiplexer #(.width(11)) multiplexer_1 (
    .in0(bit_extender_1_out), .in1(Instruction[10:0]), .out(multiplexer_1_out), .sel(Instruction[13]));
  assign Offset = multiplexer_1_out & bit_extender_2_out;  // AND_Gate and_1, 11 bits wide
  assign bit_extender_2_out = {{10{Verified}}, Verified};  // Bit_Extender bit_extender_2
  AL al_2 (.Res(al_2_res));
  NV nv_2 (.Res(nv_2_res));
  Multiplexer #(.select(4)) multiplexer_2 (
    .in0(eq_1_res), .in1(ne_1_res), .in2(cs_hs_1_res), .in3(cc_lo_1_res), .in4(mi_1_res), .in5(pl_1_res),
    .in6(vs_1_res), .in7(vc_1_res), .in8(hi_1_res), .in9(ls_1_res), .in10(ge_1_res), .in11(lt_1_res),
    .in12(gt_1_res), .in13(le_1_res), .in14(al_1_res), .in15(nv_1_res), .out(multiplexer_2_out),
    .sel(Instruction[11:8]));
  Multiplexer multiplexer_3 (.in0(al_2_res), .in1(nv_2_res), .out(multiplexer_3_out), .sel(Instruction[11]));
  and and_2 (Verified, Enable, multiplexer_4_out);
  Multiplexer #(.select(2)) multiplexer_4 (
    .in0(1'b0), .in1(multiplexer_2_out), .in2(multiplexer_3_out), .in3(1'b0), .out(multiplexer_4_out),
    .sel(Instruction[13:12]));

  // Other names for the same wires on the sheet: E = Enable; cond[3:0] = Instruction[11:8]; uncond = Instruction[11];
  //   kind[1:0] = Instruction[13:12]
endmodule

module EQ (
  input  Z,
  output Res
);


  assign Res = Z;
endmodule

module NE (
  input  Z,
  output Res
);

  not not_1 (Res, Z);
endmodule

module CS_HS (
  input  C,
  output Res
);


  assign Res = C;
endmodule

module CC_LO (
  input  C,
  output Res
);

  not not_1 (Res, C);
endmodule

module MI (
  input  N,
  output Res
);


  assign Res = N;
endmodule

module PL (
  input  N,
  output Res
);

  not not_1 (Res, N);
endmodule

module VS (
  input  V,
  output Res
);


  assign Res = V;
endmodule

module VC (
  input  V,
  output Res
);

  not not_1 (Res, V);
endmodule

module HI (
  input  C,
  input  Z,
  output Res
);

  wire not_1_out;

  not not_1 (not_1_out, Z);
  and and_1 (Res, C, not_1_out);
endmodule

module LS (
  input  C,
  input  Z,
  output Res
);

  wire not_1_out;

  not not_1 (not_1_out, C);
  or or_1 (Res, not_1_out, Z);
endmodule

module GE (
  input  N,
  input  V,
  output Res
);

  xnor xnor_1 (Res, N, V);
endmodule

module LT (
  input  N,
  input  V,
  output Res
);

  xor xor_1 (Res, N, V);
endmodule

module GT (
  input  Z,
  input  N,
  input  V,
  output Res
);

  wire not_1_out, xnor_1_out;

  not not_1 (not_1_out, Z);
  xnor xnor_1 (xnor_1_out, N, V);
  and and_1 (Res, not_1_out, xnor_1_out);
endmodule

module LE (
  input  Z,
  input  N,
  input  V,
  output Res
);

  wire xor_1_out;

  xor xor_1 (xor_1_out, N, V);
  or or_1 (Res, Z, xor_1_out);
endmodule

module AL (
  output Res
);


  assign Res = 1'b1;
endmodule

module NV (
  output Res
);


  assign Res = 1'b0;
endmodule
