// Logisim project Ctl_Data_Processing.circ as structural Verilog: 1 circuit, main circuit Data_Processing
module Data_Processing (
  input  Enable,
  input  [15:0] Instruction,
  output [2:0] Rd,
  output [2:0] Rn,
  output [2:0] Rm,
  output [3:0] ALU_Opcode,
  output [3:0] Flags_Update_Mask
);

  wire C_Mask, V_Mask;
  wire [2:0] bit_extender_1_out, Rd_t, Rm_t, Rn_t;
  wire [3:0] bit_extender_2_out;

  Multiplexer #(.select(4)) multiplexer_1 (
    .in0(1'b1), .in1(1'b1), .in2(1'b1), .in3(1'b1), .in4(1'b1), .in5(1'b1), .in6(1'b1), .in7(1'b1),
    .in8(1'b1), .in9(1'b1), .in10(1'b1), .in11(1'b1), .in12(1'b1), .in13(1'b0), .in14(1'b1), .in15(1'b1),
    .out(C_Mask), .sel(Instruction[9:6]));
  Multiplexer #(.select(4), .width(3)) multiplexer_2 (
    .in0(Instruction[5:3]), .in1(Instruction[5:3]), .in2(Instruction[5:3]), .in3(Instruction[5:3]),
    .in4(Instruction[5:3]), .in5(Instruction[5:3]), .in6(Instruction[5:3]), .in7(Instruction[5:3]),
    .in8(Instruction[5:3]), .in9(Instruction[5:3]), .in10(Instruction[5:3]), .in11(Instruction[5:3]),
    .in12(Instruction[5:3]), .in13(Instruction[2:0]), .in14(Instruction[5:3]), .in15(Instruction[5:3]),
    .out(Rm_t), .sel(Instruction[9:6]));
  Multiplexer #(.select(4)) multiplexer_3 (
    .in0(1'b0), .in1(1'b0), .in2(1'b0), .in3(1'b0), .in4(1'b0), .in5(1'b1), .in6(1'b1), .in7(1'b0),
    .in8(1'b0), .in9(1'b1), .in10(1'b1), .in11(1'b1), .in12(1'b0), .in13(1'b0), .in14(1'b0), .in15(1'b0),
    .out(V_Mask), .sel(Instruction[9:6]));
  assign bit_extender_1_out = {{2{Enable}}, Enable};  // Bit_Extender bit_extender_1
  assign bit_extender_2_out = {{3{Enable}}, Enable};  // Bit_Extender bit_extender_2
  Multiplexer #(.select(4), .width(3)) multiplexer_4 (
    .in0(Instruction[2:0]), .in1(Instruction[2:0]), .in2(Instruction[2:0]), .in3(Instruction[2:0]),
    .in4(Instruction[2:0]), .in5(Instruction[2:0]), .in6(Instruction[2:0]), .in7(Instruction[2:0]),
    .in8(Instruction[2:0]), .in9(Instruction[5:3]), .in10(Instruction[2:0]), .in11(Instruction[2:0]),
    .in12(Instruction[2:0]), .in13(Instruction[5:3]), .in14(Instruction[2:0]), .in15(Instruction[2:0]),
    .out(Rn_t), .sel(Instruction[9:6]));
  assign Rd = bit_extender_1_out & Rd_t;  // AND_Gate and_1, 3 bits wide
  assign Rn = bit_extender_1_out & Rn_t;  // AND_Gate and_2, 3 bits wide
  assign Rm = bit_extender_1_out & Rm_t;  // AND_Gate and_3, 3 bits wide
  assign ALU_Opcode = bit_extender_2_out & Instruction[9:6];  // AND_Gate and_4, 4 bits wide
  assign Flags_Update_Mask = bit_extender_2_out & {2'b11, C_Mask, V_Mask};  // AND_Gate and_5, 4 bits wide
  Multiplexer #(.select(4), .width(3)) multiplexer_5 (
    .in0(Instruction[2:0]), .in1(Instruction[2:0]), .in2(Instruction[2:0]), .in3(Instruction[2:0]),
    .in4(Instruction[2:0]), .in5(Instruction[2:0]), .in6(Instruction[2:0]), .in7(Instruction[2:0]),
    .in8(Instruction[2:0]), .in9(Instruction[2:0]), .in10(Instruction[2:0]), .in11(Instruction[2:0]),
    .in12(Instruction[2:0]), .in13(Instruction[2:0]), .in14(Instruction[2:0]), .in15(Instruction[2:0]),
    .out(Rd_t), .sel(Instruction[9:6]));

  // Other names for the same wires on the sheet: Operand_2[2:0] = Instruction[2:0];
  //   Rd_default[2:0] = Instruction[2:0]; Rn_default[2:0] = Instruction[2:0]; Operand_1[2:0] = Instruction[5:3];
  //   Rm_default[2:0] = Instruction[5:3]; ALU_opcode_t[3:0] = Instruction[9:6]

  // Notes on the sheet:
  //   Note 2: RSB instruction has Rn as 1st operand.
  //   MUL instruction has Rn as 1st operand and Rdm as 2nd operand
  //   For simplification purposes, Rm is used for 1st operand both here and in the ALU.
  //   Note: instructions that does not save the result will still have the second operand as the destination register, the ALU will copy the second register to the destination register
  //   Pull output low on Enable = 0
endmodule
