// Logisim project Ctl_Flags_APSR.circ as structural Verilog: 1 circuit, main circuit Flags_APSR
module Flags_APSR (
  input  [3:0] Update_Mask,
  input  [3:0] Flags_In,
  input  Clk,
  input  Rst,
  output [3:0] Flags_Out
);

  wire [3:0] and_1_out, and_2_out, not_1_out, or_1_out;

  assign and_1_out = Flags_Out & not_1_out;  // AND_Gate and_1, 4 bits wide
  assign not_1_out = ~Update_Mask;  // NOT_Gate not_1, 4 bits wide
  assign and_2_out = Update_Mask & Flags_In;  // AND_Gate and_2, 4 bits wide
  assign or_1_out = and_1_out | and_2_out;  // OR_Gate or_1, 4 bits wide
  D_Flip_Flop d_ff_1 (.D(or_1_out[0]), .clk(Clk), .Q(Flags_Out[0]), .reset(Rst));  // open: Qn, preset
  D_Flip_Flop d_ff_2 (.D(or_1_out[1]), .clk(Clk), .Q(Flags_Out[1]), .reset(Rst));  // open: Qn, preset
  D_Flip_Flop d_ff_3 (.D(or_1_out[2]), .clk(Clk), .Q(Flags_Out[2]), .reset(Rst));  // open: Qn, preset
  D_Flip_Flop d_ff_4 (.D(or_1_out[3]), .clk(Clk), .Q(Flags_Out[3]), .reset(Rst));  // open: Qn, preset

  // Other names for the same wires on the sheet: old_flag[3:0] = Flags_Out
endmodule
