// Logisim project Ctl_Load_Store.circ as structural Verilog: 1 circuit, main circuit Load_Store
module Load_Store (
  input  Enable,
  input  [15:0] Instruction,
  input  Clk,
  input  Reset,
  input  [31:0] Stack_Pointer,
  output Store,
  output Load,
  output PC_Hold,
  output [2:0] Rmd,
  output [31:0] RAM_Addr
);

  wire d_ff_1_qn, demultiplexer_1_out0, demultiplexer_1_out1, Load_Store_Flag, not_1_out, PC_Hold_t;
  wire [2:0] E3;
  wire [31:0] adder_1_out, bit_extender_1_out, E32, offset;

  not not_1 (not_1_out, PC_Hold_t);
  D_Flip_Flop d_ff_1 (.D(not_1_out), .clk(Clk), .Q(PC_Hold_t), .Qn(d_ff_1_qn), .reset(Reset));  // open: preset
  assign bit_extender_1_out = {{24{Instruction[7]}}, Instruction[7:0]};  // Bit_Extender bit_extender_1
  Multiplexer multiplexer_1 (.in0(1'b1), .in1(d_ff_1_qn), .out(Load_Store_Flag), .sel(Instruction[11]));
  Shifter #(.width(32)) shifter_1 (.in(bit_extender_1_out), .\dist (5'b00010), .out(offset));
  assign E3 = {{2{Enable}}, Enable};  // Bit_Extender bit_extender_2
  assign E32 = {{31{Enable}}, Enable};  // Bit_Extender bit_extender_3
  Demultiplexer demultiplexer_1 (
    .out0(demultiplexer_1_out0), .out1(demultiplexer_1_out1), .in(Load_Store_Flag), .sel(Instruction[11]));
  Adder #(.width(32)) adder_1 (.a(Stack_Pointer), .b(offset), .out(adder_1_out));  // open: cin, cout
  and and_1 (Store, Enable, demultiplexer_1_out0);
  and and_2 (Load, demultiplexer_1_out1, Enable);
  and and_3 (PC_Hold, Enable, PC_Hold_t);
  assign Rmd = E3 & Instruction[10:8];  // AND_Gate and_4, 3 bits wide
  assign RAM_Addr = E32 & adder_1_out;  // AND_Gate and_5, 32 bits wide

  // Other names for the same wires on the sheet: E1 = Enable; Rt[2:0] = Instruction[10:8]; Inst = Instruction[11];
  //   SP[31:0] = Stack_Pointer

  // Notes on the sheet:
  //   Instruction: pull=down
  //   Delay load and hold PC for 1 cycle for the RAM to send out requested data 
endmodule
