// Logisim project Ctl_Shift_Add_Sub_Mov.circ as structural Verilog
module Shift_Add_Sub_Mov (
  input  Enable,
  input  [15:0] Instruction,
  output [3:0] ALU_Opcode,
  output [3:0] Flags_Update_Mask,
  output Carry,
  output [4:0] Imm5,
  output Imm32_Enable,
  output [31:0] Imm32,
  output [2:0] Rm,
  output [2:0] Rn,
  output [2:0] Rd
);

  wire C_Mask, multiplexer_6_out, multiplexer_8_out, V_Mask;
  wire [2:0] E3, multiplexer_10_out, multiplexer_11_out, multiplexer_12_out;
  wire [3:0] ALU_Opcode_t, E4, multiplexer_1_out;
  wire [4:0] E5, multiplexer_7_out;
  wire [31:0] bit_extender_5_out, bit_extender_6_out, E32, multiplexer_5_out, multiplexer_9_out,
       negator_1_out;

  Multiplexer #(.select(2), .width(4)) multiplexer_1 (
    .in0(4'b0101), .in1(4'b0110), .in2(4'b0101), .in3(4'b0110), .out(multiplexer_1_out),
    .sel(Instruction[10:9]));
  Multiplexer #(.select(3)) multiplexer_2 (
    .in0(1'b1), .in1(1'b1), .in2(1'b1), .in3(1'b1), .in4(1'b0), .in5(1'b1), .in6(1'b1), .in7(1'b1),
    .out(C_Mask), .sel(Instruction[13:11]));
  Multiplexer #(.select(3), .width(4)) multiplexer_3 (
    .in0(4'b0010), .in1(4'b0011), .in2(4'b0100), .in3(multiplexer_1_out), .in4(4'b1001), .in5(4'b1010),
    .in6(4'b0101), .in7(4'b0110), .out(ALU_Opcode_t), .sel(Instruction[13:11]));
  Multiplexer #(.select(3)) multiplexer_4 (
    .in0(1'b0), .in1(1'b0), .in2(1'b0), .in3(1'b1), .in4(1'b0), .in5(1'b1), .in6(1'b1), .in7(1'b1),
    .out(V_Mask), .sel(Instruction[13:11]));
  assign E4 = {{3{Enable}}, Enable};  // Bit_Extender bit_extender_1
  assign E3 = {{2{Enable}}, Enable};  // Bit_Extender bit_extender_2
  assign E32 = {{31{Enable}}, Enable};  // Bit_Extender bit_extender_3
  assign E5 = {{4{Enable}}, Enable};  // Bit_Extender bit_extender_4
  assign bit_extender_5_out = {{24{1'b0}}, Instruction[7:0]};  // Bit_Extender bit_extender_5
  Negator #(.width(32)) negator_1 (.in(bit_extender_5_out), .out(negator_1_out));
  Multiplexer #(.select(2), .width(32)) multiplexer_5 (
    .in0(negator_1_out), .in1(bit_extender_5_out), .in2(bit_extender_5_out), .in3(bit_extender_5_out),
    .out(multiplexer_5_out), .sel(Instruction[12:11]));
  assign bit_extender_6_out = {{29{1'b0}}, Instruction[8:6]};  // Bit_Extender bit_extender_6
  Multiplexer multiplexer_6 (
    .in0(Instruction[9]), .in1(Instruction[11]), .out(multiplexer_6_out), .sel(Instruction[13]));
  Multiplexer #(.select(2), .width(5)) multiplexer_7 (
    .in0(Instruction[10:6]), .in1(Instruction[10:6]), .in2(Instruction[10:6]), .in3({5{1'b0}}),
    .out(multiplexer_7_out), .sel(Instruction[12:11]));
  Multiplexer multiplexer_8 (
    .in0(Instruction[10]), .in1(Instruction[13]), .out(multiplexer_8_out), .sel(Instruction[13]));
  Multiplexer #(.width(32)) multiplexer_9 (
    .in0(bit_extender_6_out), .in1(multiplexer_5_out), .out(multiplexer_9_out), .sel(Instruction[13]));
  Multiplexer #(.width(3)) multiplexer_10 (
    .in0(Instruction[8:6]), .in1(Instruction[10:8]), .out(multiplexer_10_out), .sel(Instruction[13]));
  Multiplexer #(.width(3)) multiplexer_11 (
    .in0(Instruction[5:3]), .in1(Instruction[10:8]), .out(multiplexer_11_out), .sel(Instruction[13]));
  Multiplexer #(.width(3)) multiplexer_12 (
    .in0(Instruction[2:0]), .in1(Instruction[10:8]), .out(multiplexer_12_out), .sel(Instruction[13]));
  assign ALU_Opcode = E4 & ALU_Opcode_t;  // AND_Gate and_1, 4 bits wide
  assign Flags_Update_Mask = E4 & {2'b11, C_Mask, V_Mask};  // AND_Gate and_2, 4 bits wide
  and and_3 (Carry, Enable, multiplexer_6_out);
  assign Imm5 = E5 & multiplexer_7_out;  // AND_Gate and_4, 5 bits wide
  and and_5 (Imm32_Enable, Enable, multiplexer_8_out);
  assign Imm32 = E32 & multiplexer_9_out;  // AND_Gate and_6, 32 bits wide
  assign Rm = E3 & multiplexer_10_out;  // AND_Gate and_7, 3 bits wide
  assign Rn = E3 & multiplexer_11_out;  // AND_Gate and_8, 3 bits wide
  assign Rd = E3 & multiplexer_12_out;  // AND_Gate and_9, 3 bits wide

  // Other names for the same wires on the sheet: E1 = Enable; Operand_3[2:0] = Instruction[2:0];
  //   Operand_2[2:0] = Instruction[5:3]; Operand_1[2:0] = Instruction[8:6]; Operand_Default[2:0] = Instruction[10:8];
  //   tenine[1:0] = Instruction[10:9]; main_opcode[2:0] = Instruction[13:11]

  // Notes on the sheet:
  //   Pull output low on Enable = 0
  //   Enable carry for SUB since it is reversed in ALU
  //   only ADD and SUB use Rm
  //   ALU will use Imm32 instead of Rm
  //   Note: ALU uses Rn register for shifts. Use Rn instead of Rm for shifts (immediate) here too
  //   Note 2: MOV uses RSB ALU opcode with Imm8 reversed so that it is copied to output register
  //   Note 3: Imm32_Enable forces the use of the immediate for Rm register
endmodule

module Alu_Opcode (
  input  thirteen,
  input  twelve,
  input  eleven,
  input  ten,
  input  nine,
  output first,
  output second,
  output third,
  output forth
);

  wire and_2_out, and_3_out, and_4_out, and_5_out, and_6_out, and_7_out, not_1_out, not_2_out, not_3_out,
       not_4_out;

  not not_1 (not_1_out, thirteen);
  not not_2 (not_2_out, twelve);
  not not_3 (not_3_out, eleven);
  not not_4 (not_4_out, nine);
  and and_1 (first, thirteen, not_2_out);
  and and_2 (and_2_out, thirteen, not_3_out);
  and and_3 (and_3_out, eleven, nine);
  and and_4 (and_4_out, thirteen, eleven);
  and and_5 (and_5_out, thirteen, not_3_out);
  and and_6 (and_6_out, not_1_out, not_2_out, eleven);
  and and_7 (and_7_out, not_1_out, eleven, not_4_out);
  or or_1 (second, twelve, and_2_out);
  or or_2 (third, not_2_out, and_3_out, and_4_out);
  or or_3 (forth, and_5_out, and_6_out, and_7_out);
endmodule
